# Fritzing sketch ESP06 (saved by Fritzing 0.9.3b)
breadboards: 1

parts:
  U1 = ESP8266 WiFi Module [part_number=ESP8266]
  DS1 = DS18B20 1-Wire Temperature Sensor [part_number=DS18B20]
  DS2 = DS18B20 1-Wire Temperature Sensor [part_number=DS18B20]
  IC1 = Voltage Regulator LM1117 [package=sot223]
  HLK-PM1 = HLK-PM01
  C1 = Capacitor Polarized [package=cpol-radial-100uf-25v]
  R1 = Resistor [tolerance=±5% resistance=4.7k package=THT]
  R2 = Resistor [tolerance=±5% resistance=4.7k package=THT]
  R3 = Resistor [tolerance=±5% resistance=4.7k package=THT]
  R4 = Resistor [tolerance=±5% resistance=4.7k package=THT]
  JP1 = Header 5 [package=1x05-1mm-ra]
  S1 = Pushbutton [package="[SMD]"]
  S2 = Pushbutton [package="[SMD]"]
  JP2 = Header 5 [package=1x05-1mm-ra]
  hc-sr1 = hc-sr04

nets:
  N1: U1.RXD, JP1.2
  N2: U1.VCC, U1.CH_PD, C1.+, R1.Pin_1, R2.Pin_1, R3.Pin_1, JP1.1
  N3: U1.GPIO_0, R1.Pin_0, S1.Pin_3, S1.Pin_4
  N4: U1.GPIO_2, R3.Pin_0
  N5: U1.GND, U1.GPIO_15, C1.-, JP1.5
  N6: U1.TXD, JP1.3
  N7: U1.GPIO_5, JP1.4
  N8: U1.REST, R2.Pin_0, S2.Pin_1, S2.Pin_2
  GND: DS1.GND, DS2.GND, IC1.ADJ, HLK-PM1.-Vo, JP2.1, hc-sr1.GND
  N9: DS1.DQ, DS2.DQ, R4.Pin_1, JP2.4
  VDD: DS1.VDD, DS2.VDD, IC1.OUT, R4.Pin_0, JP2.5, hc-sr1.VCC
  N10: IC1.IN, HLK-PM1.+Vo
  N11: S1.Pin_1, S1.Pin_2, S2.Pin_3, S2.Pin_4
  N12: JP2.2, hc-sr1.Echo
  N13: JP2.3, hc-sr1.Trig
